// Logisim project stargate323_LogisimEvolution.circ as structural Verilog: 1 circuit, main circuit main
module main (
);

  wire clk_out, d_ff_1_q, d_ff_2_qn, d_ff_3_q, d_ff_4_q, d_ff_5_q, d_ff_6_q, d_ff_7_q, d_ff_8_q, d_ff_9_q,
       d_ff_10_q, d_ff_11_q, d_ff_12_q, d_ff_13_q, d_ff_14_q, d_ff_15_q, d_ff_16_q, d_ff_17_q, n7474_1_pin5,
       n74283_1_pin7, not_1_out, not_2_out, not_3_out, not_4_out, not_5_out, not_6_out, not_7_out, RESET_out;
  wire [7:0] counter_1_q, counter_2_q, counter_3_q, multiplexer_1_out, multiplexer_2_out, n74283_2_pin4,
       P0807_data, P0808_data, P0810_data, P0811_data, register_1_q, TIMING_q;
  wire [8:8] n7474_1_pin2;
  wire [11:5] MOD_CNT_p1;
  wire [12:6] PDL_p1;

  Clock sysclk ();  // open: out
  Clock #(.highDuration(4), .lowDuration(4)) clk (.out(clk_out));
  Counter TIMING (.up(1'b1), .count(1'b1), .clk(clk_out), .Q(TIMING_q));  // open: clr, load, D, carry
  ROM P0810 (.addr(TIMING_q), .data(P0810_data));
  ROM P0811 (.addr(TIMING_q), .data(P0811_data));
  not not_1 (not_1_out, TIMING_q[1]);
  D_Flip_Flop d_ff_1 (.D(not_1_out), .clk(clk_out), .Q(d_ff_1_q));  // open: Qn, preset, reset
  D_Flip_Flop d_ff_2 (.D(P0810_data[0]), .clk(clk_out), .Qn(d_ff_2_qn));  // open: Q, preset, reset
  D_Flip_Flop d_ff_3 (.D(P0810_data[1]), .clk(clk_out), .Q(d_ff_3_q));  // open: Qn, preset, reset
  D_Flip_Flop d_ff_4 (.D(P0810_data[2]), .clk(clk_out), .Q(d_ff_4_q));  // open: Qn, preset, reset
  D_Flip_Flop d_ff_5 (.D(P0810_data[3]), .clk(clk_out), .Q(d_ff_5_q));  // open: Qn, preset, reset
  D_Flip_Flop d_ff_6 (.D(P0810_data[4]), .clk(clk_out), .Q(d_ff_6_q));  // open: Qn, preset, reset
  D_Flip_Flop d_ff_7 (.D(P0810_data[5]), .clk(clk_out), .Q(d_ff_7_q));  // open: Qn, preset, reset
  D_Flip_Flop d_ff_8 (.D(P0810_data[6]), .clk(clk_out), .Q(d_ff_8_q));  // open: Qn, preset, reset
  D_Flip_Flop d_ff_9 (.D(P0810_data[7]), .clk(clk_out), .Q(d_ff_9_q));  // open: Qn, preset, reset
  D_Flip_Flop d_ff_10 (.D(P0811_data[0]), .clk(clk_out), .Q(d_ff_10_q));  // open: Qn, preset, reset
  D_Flip_Flop d_ff_11 (.D(P0811_data[1]), .clk(clk_out), .Q(d_ff_11_q));  // open: Qn, preset, reset
  D_Flip_Flop d_ff_12 (.D(P0811_data[2]), .clk(clk_out), .Q(d_ff_12_q));  // open: Qn, preset, reset
  D_Flip_Flop d_ff_13 (.D(P0811_data[3]), .clk(clk_out), .Q(d_ff_13_q));  // open: Qn, preset, reset
  D_Flip_Flop d_ff_14 (.D(P0811_data[4]), .clk(clk_out), .Q(d_ff_14_q));  // open: Qn, preset, reset
  D_Flip_Flop d_ff_15 (.D(P0811_data[5]), .clk(clk_out), .Q(d_ff_15_q));  // open: Qn, preset, reset
  D_Flip_Flop d_ff_16 (.D(P0811_data[6]), .clk(clk_out), .Q(d_ff_16_q));  // open: Qn, preset, reset
  D_Flip_Flop d_ff_17 (.D(P0811_data[7]), .clk(clk_out), .Q(d_ff_17_q));  // open: Qn, preset, reset
  not not_2 (not_2_out, d_ff_1_q);
  // Probe on d_ff_2_qn
  Counter counter_1 (
    .clr(d_ff_2_qn), .up(1'b1), .count(1'b1), .clk(not_3_out), .Q(counter_1_q));  // open: load, D, carry
  not not_3 (not_3_out, not_2_out);
  // Probe on d_ff_3_q
  not not_4 (not_4_out, d_ff_3_q);
  // Probe on d_ff_4_q
  // Probe on d_ff_5_q
  // Probe on d_ff_6_q
  // Probe on d_ff_7_q
  // Probe on d_ff_8_q
  // Probe on d_ff_9_q
  // Probe on d_ff_10_q
  // Probe on d_ff_11_q
  // Probe on d_ff_12_q
  // Probe on d_ff_13_q
  // Probe on d_ff_14_q
  // Probe on d_ff_15_q
  // Probe on d_ff_16_q
  // Probe on d_ff_17_q
  // Probe on not_4_out
  // Probe on d_ff_1_q
  // Probe on counter_1_q[0]
  // Probe on counter_1_q[1]
  // Probe on counter_1_q[2]
  // Probe on counter_1_q[3]
  // Probe on counter_1_q[4]
  // Probe on counter_1_q[5]
  // DipSwitch #(.number(7)) MOD_CNT: pin names not known; wires that end beside it: MOD_CNT_p1[5], MOD_CNT_p1[6], MOD_CNT_p1[7], MOD_CNT_p1[8], MOD_CNT_p1[9], MOD_CNT_p1[10], MOD_CNT_p1[11]
  Button RESET (.out(RESET_out));
  not not_5 (not_5_out, counter_1_q[5]);
  not not_6 (not_6_out, not_5_out);
  // DipSwitch #(.number(4)) PDL: pin names not known; wires that end beside it: PDL_p1[6], PDL_p1[7], PDL_p1[8], PDL_p1[12]
  ROM #(.addrWidth(12)) P0807 (.addr({MOD_CNT_p1, counter_1_q[5:1]}), .data(P0807_data));
  Counter #(.trigger("falling")) counter_2 (
    .clr(RESET_out), .up(1'b1), .count(1'b1), .clk(counter_3_q[7]), .Q(counter_2_q));  // open: load, D, carry
  Counter #(.trigger("falling")) counter_3 (
    .clr(RESET_out), .up(1'b1), .count(1'b1), .clk(not_6_out), .Q(counter_3_q));  // open: load, D, carry
  // DipSwitch #(.number(3)) PGM: pin names not known; wires that end beside it: PDL_p1[9], PDL_p1[10], PDL_p1[11]
  ROM #(.addrWidth(13)) P0808 (.addr({PDL_p1, counter_1_q[5:0]}), .data(P0808_data));
  // Probe on counter_3_q
  // Probe on P0807_data
  // Probe on counter_2_q
  Multiplexer #(.enable("false"), .width(8)) multiplexer_1 (
    .in0(counter_3_q), .in1(counter_2_q), .out(multiplexer_1_out), .sel(counter_1_q[0]));
  // Probe on P0808_data
  // Probe on multiplexer_2_out
  Multiplexer #(.enable("false"), .width(8)) multiplexer_2 (
    .in0(P0808_data), .in1(P0807_data), .out(multiplexer_2_out), .sel(not_7_out));
  // Probe on not_7_out
  not not_7 (not_7_out, d_ff_9_q);
  Register register_1 (.D(multiplexer_2_out), .en(1'b1), .clk(d_ff_1_q), .Q(register_1_q));  // open: clr
  // Probe on multiplexer_1_out
  // Probe on register_1_q
  // Probe on TIMING_q
  // Probe on multiplexer_1_out
  _7474 #(.ShowInternalStructure("true")) u_7474_1 (
    .pin1(d_ff_6_q), .pin2(n7474_1_pin2[8]), .pin3(d_ff_1_q), .pin5(n7474_1_pin5));  // open: pin4, pin6, pin13, pin12, pin11, pin10, pin9, pin8
  _74283 #(.ShowInternalStructure("true")) u_74283_1 (
    .pin1(n74283_2_pin4[6]), .pin2(register_1_q[5]), .pin3(multiplexer_1_out[5]), .pin4(n74283_2_pin4[5]),
    .pin5(multiplexer_1_out[4]), .pin6(register_1_q[4]), .pin7(n74283_1_pin7), .pin15(register_1_q[6]),
    .pin14(multiplexer_1_out[6]), .pin13(n74283_2_pin4[0]), .pin12(multiplexer_1_out[7]),
    .pin11(register_1_q[7]), .pin10(n74283_2_pin4[7]), .pin9(n7474_1_pin2[8]));
  _74283 #(.ShowInternalStructure("true")) u_74283_2 (
    .pin1(n74283_2_pin4[2]), .pin2(register_1_q[1]), .pin3(multiplexer_1_out[1]), .pin4(n74283_2_pin4[1]),
    .pin5(multiplexer_1_out[0]), .pin6(register_1_q[0]), .pin7(n7474_1_pin5), .pin15(register_1_q[2]),
    .pin14(multiplexer_1_out[2]), .pin13(n74283_2_pin4[3]), .pin12(multiplexer_1_out[3]),
    .pin11(register_1_q[3]), .pin10(n74283_2_pin4[4]), .pin9(n74283_1_pin7));
  // Probe on n74283_2_pin4
  // Probe on {n74283_2_pin4[7], n74283_2_pin4[0], n74283_2_pin4[6:1]}
  // Probe on {n7474_1_pin2[8], n74283_2_pin4[7], n74283_2_pin4[0], n74283_2_pin4[6:1]}

  // Notes on the sheet:
  //   contents of P0810 (hex, n*v repeats v):
  //   e4 e4 e4 e5 e5 c5 5*e5 c5 4*e5 c5 e5 e5 e5 c5 e5 e5 e5 c5 e5 e5 c5 e5 e5 c5 e5 85 a5 e5 e5 e5 c5 e5
  //   e5 e5 c5 e5 e5 e5 c5 e5 e5 e5 c5 e5 e5 c5 e5 e5 c5 e5 e5 d5 f5 75 55 75 7d fb 9b a3 f3 73 73 7b 7b
  //   ff fb e3 f3 73 73 7b 7b ff fb e3 f3 73 73 7b 7b ff fb e3 f3 73 73 7b 7b ff fb e3 f3 73 73 7b 7b ff
  //   fb e3 f3 73 73 7b 7b ff fb e3 f3 73 73 7b 7b ff fb e3 f3 73 73 7b 7b ff fb e3 f3 73 73 7b 7b ff fb
  //   e3 f3 73 73 7b 7b ff fb e3 f3 73 73 7b 7b ff fb e3 f3 73 73 7b 7b ff fb e3 f3 73 73 7b 7b ff fb e3
  //   f3 73 73 7b 7b ff fb e3 f3 f3 f3 fb fb ff fb e3 f3 f3 f3 fb fb ff fb e3 f3 f3 f3 fb fb ff fb e3 f3
  //   f3 f3 fb fb ff fb e3 f3 f3 f3 fb fb ff fb e3 f3 f3 f3 fb fb ff fb e3 f3 f3 f3 fb fb ff fb e3 f3 f3
  //   f3 fb fb ff fb e3 f3 f3 f3 fb fb ff fb e3 e3 eb e2 c2 e2
  //   contents of P0811 (hex, n*v repeats v):
  //   32*7d 24*bd 8*bc 4*3e 4*1e 4*3e 4*2e 4*3e 4*2e 4*3e 4*2e 4*3e 4*2e 4*3e 4*2e 4*3e 4*2e 4*3e 4*2e
  //   4*3e 4*2e 4*3e 4*2e 4*3e 4*2e 4*3e 4*2e 4*3e 4*2e 4*3e 4*2e 4*3e 4*2e 4*3e 4*2e 4*3e 4*36 4*3e 4*36
  //   3e 3c 3c 3c 4*34 4*3c 4*34 4*3c 4*38 4*3c 4*38 4*3c 4*38 4*3d 4*39
  //   contents of P0807 (hex, n*v repeats v):
  //   6*ff 2e ed a9 5c 35 ef 4 ac 72 a6 3c ad 1e ed ae e5 16*ff 2e ed 8e 5c 35 ef 4 ac e a6 3c ad 1e ed ae
  //   e5 16*ff 8a ed 8e 5c 35 ef 4 ac e a6 3c ad 1e ed ae e5 16*ff 8a ed 8e 5c 35 ef a4 ac e a6 3c 24 1e
  //   ed ae e5 16*ff 8a ed 8e 5c 35 ef a4 ac e a6 3c 24 1e 81 2b e5 16*ff 8a ed 8e 5c 35 35 a4 ac e e8 3c
  //   24 1e 81 2b e5 16*ff 8a e8 8e 5c 35 35 a4 ac e e8 3c 24 1e 81 2b fc 16*ff 8a e8 8e 5c 35 35 a4 64 e
  //   e8 3c 24 1e 81 2b fc 16*ff 8a e8 8e 5c 35 35 a4 64 e e8 45 24 3b 81 2b fc 16*ff 8a e8 e7 15 35 35 a4
  //   64 e e8 45 24 3b 81 2b fc 16*ff 8a e8 e7 15 87 35 a4 64 e e8 45 24 3b 81 2b fc 16*ff 8a e8 e7 15 87
  //   35 a4 64 a9 e8 45 24 3b 81 2b fc 16*ff 8a e8 e7 15 87 35 e9 64 a9 e8 45 24 3b 81 91 fc 16*ff 31 e8
  //   e7 15 87 55 e9 64 a9 e8 45 24 3b 81 91 fc 16*ff 31 ff e7 15 87 55 e9 64 a9 e8 45 3b 3b 81 91 fc
  //   16*ff 31 ff e7 15 87 55 e9 64 a9 e8 45 3b 3b 8 91 fc 16*ff 31 ff e7 15 87 55 e9 64 a9 b9 45 3b 4b 8
  //   91 fc 16*ff 31 ff e7 41 87 55 e9 d3 a9 b9 45 3b 4b 8 91 fc 16*ff 31 ff e7 41 87 55 e9 d3 a9 b9 45 3b
  //   4b 8 91 cf 16*ff 31 ff e7 41 87 55 e9 d3 a9 b9 ef 3b 4b 8 91 cf 16*ff 31 ff e7 41 a 55 e9 d3 a9 b9
  //   ef 3b 4b 8 91 cf 16*ff 31 ff 2b 41 a 55 4a d3 a9 b9 ef 3b 4b 8 91 cf 16*ff 31 ff 2b 41 a 55 4a d3 1b
  //   b9 ef 3b 4b 8 91 cf 16*ff 32 ff 2b 41 a 55 4a d3 1b b9 ef 3b 4b 8 a1 cf 16*ff 32 ff 2b 41 a e5 4a d3
  //   1b b9 ef f 4b 8 a1 cf 16*ff 32 22 2b 41 a e5 4a d3 1b b9 ef f 4b 6 a1 cf 16*ff 32 22 2b 41 a e5 4a
  //   d3 1b d6 ef f db 6 a1 cf 16*ff 32 22 2b a a e5 4a e4 1b d6 ef f db 6 a1 cf 16*ff 32 22 2b a a e5 4a
  //   e4 1b d6 ef f db 6 a1 44 16*ff 32 22 2b a 64 e5 4a e4 1b d6 ef f db 6 a1 44 16*ff 32 22 2b a 64 e5
  //   4a e4 10 d6 ef f db 6 a1 44 16*ff 32 22 4e a 64 e5 4a e4 10 d6 ef f db 6 a1 44 16*ff 32 22 4e a 64
  //   e5 65 e4 10 d6 ef 61 db 6 a1 44 16*ff 86 22 4e a 64 e5 65 e4 10 d6 ef 61 db 6 c7 44 16*ff 86 22 4e a
  //   64 36 65 e4 10 d6 ef 61 db 4b c7 44 16*ff 86 70 4e a 64 36 65 68 10 d6 ef 61 db 4b c7 44 16*ff 86 70
  //   4e a 64 36 65 68 10 cd ef 61 69 4b c7 44 16*ff 86 70 4e 8b 64 36 65 68 10 cd ef 61 69 4b c7 44 16*ff
  //   86 70 4e 8b 50 36 65 68 10 cd ef 61 69 4b c7 6d 16*ff 86 70 4e 8b 50 36 65 68 10 cd 6c 61 69 4b c7
  //   6d 16*ff 86 70 4e 8b 50 36 65 68 3e cd 6c 61 69 4b c7 6d 16*ff 86 70 c4 8b 50 36 65 68 3e cd 6c 61
  //   69 4b c7 6d 16*ff 86 70 c4 8b 50 36 26 68 3e cd 6c 61 69 4b b5 6d 16*ff f9 70 c4 8b 50 36 26 68 3e
  //   cd 6c 61 69 4b b5 6d 16*ff f9 70 c4 8b 50 f1 26 68 3e cd 6c 3c 69 4b b5 6d 16*ff f9 b1 c4 8b 50 f1
  //   26 68 3e cd 6c 3c 69 29 b5 6d 16*ff f9 b1 c4 8b 50 f1 26 68 3e a1 6c 3c 85 29 b5 6d 16*ff f9 b1 c4
  //   d1 50 f1 26 4f 3e a1 6c 3c 85 29 b5 6d 16*ff f9 b1 c4 d1 50 f1 26 4f 3e a1 6c 3c 85 29 b5 28 16*ff
  //   f9 b1 c4 d1 de f1 26 4f 3e a1 61 3c 85 29 b5 28 16*ff f9 b1 c4 d1 de f1 78 4f 4e a1 61 3c 85 29 b5
  //   28 16*ff f9 b1 18 d1 de f1 78 4f 4e a1 61 3c 85 29 b5 28 16*ff d8 b1 18 d1 de f1 78 4f 4e a1 61 3c
  //   85 29 70 28 16*ff d8 b1 18 d1 de 6f 78 4f 4e a1 61 3c 85 55 70 28 16*ff d8 b5 18 d1 de 6f 78 4f 4e
  //   a1 61 e 85 55 70 28 16*ff d8 b5 18 d1 de 6f 78 81 4e a1 61 e 85 55 70 28 16*ff d8 b5 18 d1 de 6f 78
  //   81 4e 35 61 e a7 55 70 28 16*ff d8 b5 18 ae de 6f 78 81 4e 35 61 e a7 55 70 1e 16*ff d8 b5 18 ae de
  //   6f 78 81 4e 35 81 e a7 55 70 1e 16*ff d8 b5 18 ae 80 6f 78 81 4e 35 81 e a7 55 70 1e 16*ff d8 b5 18
  //   ae 80 6f 78 81 9a 35 81 e a7 55 70 1e 16*ff d8 b5 80 ae 80 6f 78 81 9a 35 81 e a7 55 70 1e 16*ff 5a
  //   b5 80 ae 80 6f 65 81 9a 35 81 e a7 55 70 1e 16*ff 5a b5 80 ae 80 6f 65 81 9a 35 81 42 a7 55 19 1e
  //   16*ff 5a b5 80 ae 80 4 65 81 9a 35 81 42 a7 31 19 1e 16*ff 5a 7a 80 ae 80 4 65 81 9a 8 81 42 a7 31
  //   19 1e 16*ff 5a 7a 80 ae 80 4 65 c5 9a 8 81 42 6e 31 19 1e 16*ff 5a 7a 80 9b 80 4 65 c5 9a 8 81 42 6e
  //   31 19 8 16*ff 5a 7a 80 9b 80 4 65 c5 9a 8 d5 42 6e 31 19 8 16*ff 5a 7a 80 9b f 4 65 c5 9a 8 d5 42 6e
  //   31 19 8 16*ff 5a 7a 80 9b f 4 65 c5 d8 8 d5 42 6e 31 19 8 16*ff 5a 7a 2d 9b f 4 83 c5 d8 8 d5 42 6e
  //   31 19 8 16*ff f6 7a 2d 9b f 4 83 c5 d8 8 d5 42 6e 31 19 8 16*ff f6 7a 2d 9b f 4 83 c5 d8 8 d5 27 6e
  //   31 2f 8 16*ff f6 a0 2d 9b f bc 83 c5 d8 8 d5 27 6e 31 2f 8 16*ff f6 a0 2d 9b f bc 83 c5 d8 8 d5 27
  //   fa 3b 2f 8 16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
  //   contents of P0808 (hex, n*v repeats v):
  //   16*0 5 0 7 0 9 0 b 0 e 0 10 0 14 0 16 0 17 0 19 0 1c 0 1f 0 21 0 23 0 25 90 6 40 5 f0 3 a0 2 c0 9 80
  //   7 40 5 0 3 19*0 5 0 7 0 9 0 b 0 e 0 10 0 14 0 16 0 17 0 19 0 1c 0 1f 0 21 0 23 0 25 d0 7 80 6 30 5
  //   e0 3 0 b c0 8 80 6 40 4 19*0 5 0 7 0 9 0 b 0 e 0 10 0 14 0 16 0 17 0 19 0 1c 0 1f 0 21 0 23 0 25 50
  //   5 0 4 b0 2 60 1 80 8 40 6 0 4 c0 1 19*0 5 0 7 0 9 0 b 0 e 0 10 0 14 0 16 0 17 0 19 0 1c 0 1f 0 21 0
  //   23 0 25 10 4 c0 2 70 1 20 0 40 7 0 5 c0 2 80 20*0 5 0 7 0 9 0 b 0 e 0 10 0 14 0 16 0 17 0 19 0 1c 0
  //   1f 0 21 0 23 0 25 50 a 0 9 b0 7 60 6 80 d 40 b 0 9 c0 6 19*0 5 0 7 0 9 0 b 0 e 0 10 0 14 0 16 0 17 0
  //   19 0 1c 0 1f 0 21 0 23 0 25 10 9 c0 7 70 6 20 5 40 c 0 a c0 7 80 5 19*0 5 0 7 0 9 0 b 0 e 0 10 0 14
  //   0 16 0 17 0 19 0 1c 0 1f 0 21 0 23 0 25 90 b 40 a f0 8 a0 7 c0 e 80 c 40 a 0 8 19*0 5 0 7 0 9 0 b 0
  //   e 0 10 0 14 0 16 0 17 0 19 0 1c 0 1f 0 21 0 23 0 25 10 e c0 c 70 b 20 a 40 11 0 f c0 c 80 a 19*0 8 0
  //   a 0 b 0 10 0 11 0 15 0 16 0 19 0 1c 0 1f 0 22 0 24 0 27 0 2a 0 2c e0 7 20 6 60 4 a0 2 20 c 20 9 20 6
  //   20 3 19*0 8 0 a 0 b 0 10 0 11 0 15 0 16 0 19 0 1c 0 1f 0 22 0 24 0 27 0 2a 0 2c 20 9 60 7 a0 5 e0 3
  //   60 d 60 a 60 7 60 4 19*0 8 0 a 0 b 0 10 0 11 0 15 0 16 0 19 0 1c 0 1f 0 22 0 24 0 27 0 2a 0 2c a0 6
  //   e0 4 20 3 60 1 e0 a e0 7 e0 4 e0 1 19*0 8 0 a 0 b 0 10 0 11 0 15 0 16 0 19 0 1c 0 1f 0 22 0 24 0 27
  //   0 2a 0 2c 60 5 a0 3 e0 1 20 0 a0 9 a0 6 a0 3 a0 20*0 8 0 a 0 b 0 10 0 11 0 15 0 16 0 19 0 1c 0 1f 0
  //   22 0 24 0 27 0 2a 0 2c a0 b e0 9 20 8 60 6 e0 f e0 c e0 9 e0 6 19*0 8 0 a 0 b 0 10 0 11 0 15 0 16 0
  //   19 0 1c 0 1f 0 22 0 24 0 27 0 2a 0 2c 60 a a0 8 e0 6 20 5 a0 e a0 b a0 8 a0 5 19*0 8 0 a 0 b 0 10 0
  //   11 0 15 0 16 0 19 0 1c 0 1f 0 22 0 24 0 27 0 2a 0 2c e0 c 20 b 60 9 a0 7 20 11 20 e 20 b 20 8 19*0 8
  //   0 a 0 b 0 10 0 11 0 15 0 16 0 19 0 1c 0 1f 0 22 0 24 0 27 0 2a 0 2c 60 f a0 d e0 b 20 a a0 13 a0 10
  //   a0 d a0 a 19*0 3 0 5 0 6 0 8 0 b 0 c 0 e 0 11 0 12 0 14 0 17 0 18 0 19 0 1d 0 1e 40 5 60 4 80 3 a0 2
  //   60 7 e0 5 60 4 e0 2 19*0 3 0 5 0 6 0 8 0 b 0 c 0 e 0 11 0 12 0 14 0 17 0 18 0 19 0 1d 0 1e 80 6 a0 5
  //   c0 4 e0 3 a0 8 20 7 a0 5 20 4 19*0 3 0 5 0 6 0 8 0 b 0 c 0 e 0 11 0 12 0 14 0 17 0 18 0 19 0 1d 0 1e
  //   0 4 20 3 40 2 60 1 20 6 a0 4 20 3 a0 1 19*0 3 0 5 0 6 0 8 0 b 0 c 0 e 0 11 0 12 0 14 0 17 0 18 0 19
  //   0 1d 0 1e c0 2 e0 1 0 1 20 0 e0 4 60 3 e0 1 60 20*0 3 0 5 0 6 0 8 0 b 0 c 0 e 0 11 0 12 0 14 0 17 0
  //   18 0 19 0 1d 0 1e 0 9 20 8 40 7 60 6 20 b a0 9 20 8 a0 6 19*0 3 0 5 0 6 0 8 0 b 0 c 0 e 0 11 0 12 0
  //   14 0 17 0 18 0 19 0 1d 0 1e c0 7 e0 6 0 6 20 5 e0 9 60 8 e0 6 60 5 19*0 3 0 5 0 6 0 8 0 b 0 c 0 e 0
  //   11 0 12 0 14 0 17 0 18 0 19 0 1d 0 1e 40 a 60 9 80 8 a0 7 60 c e0 a 60 9 e0 7 19*0 3 0 5 0 6 0 8 0 b
  //   0 c 0 e 0 11 0 12 0 14 0 17 0 18 0 19 0 1d 0 1e c0 c e0 b 0 b 20 a e0 e 60 d e0 b 60 a 19*0 2 0 4 0
  //   5 0 7 0 8 0 9 0 b 0 d 0 e 0 f 0 10 0 12 0 14 0 15 0 16 f0 3 80 3 10 3 a0 2 0 5 40 4 80 3 c0 2 19*0 2
  //   0 4 0 5 0 7 0 8 0 9 0 b 0 d 0 e 0 f 0 10 0 12 0 14 0 15 0 16 30 5 c0 4 50 4 e0 3 40 6 80 5 c0 4 0 4
  //   19*0 2 0 4 0 5 0 7 0 8 0 9 0 b 0 d 0 e 0 f 0 10 0 12 0 14 0 15 0 16 b0 2 40 2 d0 1 60 1 c0 3 0 3 40
  //   2 80 1 19*0 2 0 4 0 5 0 7 0 8 0 9 0 b 0 d 0 e 0 f 0 10 0 12 0 14 0 15 0 16 70 1 0 1 90 0 20 0 80 2
  //   c0 1 0 1 40 20*0 2 0 4 0 5 0 7 0 8 0 9 0 b 0 d 0 e 0 f 0 10 0 12 0 14 0 15 0 16 b0 7 40 7 d0 6 60 6
  //   c0 8 0 8 40 7 80 6 19*0 2 0 4 0 5 0 7 0 8 0 9 0 b 0 d 0 e 0 f 0 10 0 12 0 14 0 15 0 16 70 6 0 6 90 5
  //   20 5 80 7 c0 6 0 6 40 5 19*0 2 0 4 0 5 0 7 0 8 0 9 0 b 0 d 0 e 0 f 0 10 0 12 0 14 0 15 0 16 f0 8 80
  //   8 10 8 a0 7 0 a 40 9 80 8 c0 7 19*0 2 0 4 0 5 0 7 0 8 0 9 0 b 0 d 0 e 0 f 0 10 0 12 0 14 0 15 0 16
  //   70 b 0 b 90 a 20 a 80 c c0 b 0 b 40 a 19*0 f 0 10 0 11 0 14 0 15 0 19 0 1c 0 20 0 24 0 28 0 2c 0 2f
  //   0 34 0 3b 0 3f 80 a e0 7 40 5 a0 2 e0 10 60 c e0 7 60 3 19*0 f 0 10 0 11 0 14 0 15 0 19 0 1c 0 20 0
  //   24 0 28 0 2c 0 2f 0 34 0 3b 0 3f c0 b 20 9 80 6 e0 3 20 12 a0 d 20 9 a0 4 19*0 f 0 10 0 11 0 14 0 15
  //   0 19 0 1c 0 20 0 24 0 28 0 2c 0 2f 0 34 0 3b 0 3f 40 9 a0 6 0 4 60 1 a0 f 20 b a0 6 20 2 19*0 f 0 10
  //   0 11 0 14 0 15 0 19 0 1c 0 20 0 24 0 28 0 2c 0 2f 0 34 0 3b 0 3f 0 8 60 5 c0 2 20 0 60 e e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
endmodule
